# Fritzing sketch Proyecto_002 (saved by Fritzing 0.9.3b)
breadboards: 1

parts:
  Componente1 = Arduino Uno (Rev3)
  S1 = Pushbutton [package="[THT]"]
  LED1 = LED - 5mm [color="Yellow (592nm)" package="5 mm [THT]"]
  R1 = Resistor [tolerance=±5% resistance=220 package=THT]
  LED2 = LED - 5mm [color="Yellow (595nm)" package="5 mm [THT]"]
  R2 = Resistor [tolerance=±5% resistance=220 package=THT]
  S2 = Toggle Switch [package=THT]
  R3 = Resistor [tolerance=±5% resistance=1k package=THT]
  R4 = Resistor [tolerance=±5% resistance=1k package=THT]
  R5 = Resistor [tolerance=±5% resistance=1k package=THT]

nets:
  N1: Componente1.D2, LED2.anode
  N2: Componente1.D3_PWM, LED1.anode
  N3: Componente1.D4, S2.L2, R5.Pin_1
  N4: Componente1.D5_PWM, S2.L1, R4.Pin_1
  N5: Componente1.D6_PWM, S1.Pin_1, S1.Pin_2, R3.Pin_1
  N6: S1.Pin_3, S1.Pin_4, S2.COM
  N7: LED1.cathode, R1.Pin_0
  N8: R1.Pin_1, R2.Pin_1, R3.Pin_0, R4.Pin_0, R5.Pin_0
  N9: LED2.cathode, R2.Pin_0
